// Digital circuit cpu.dig as structural Verilog
module cpu (
  input  clk,
  input  clk_2,
  input  RESET
);

  wire nand_1_out, nand_4_out, nand_5_out, nand_6_out, oprom_1_bssel, oprom_1_fwen, oprom_1_massel,
       oprom_1_mwen, oprom_1_rwen;
  wire [1:0] nand_2_out, oprom_1_pcssel, oprom_1_rssel;
  wire [2:0] program_memory_1_aluop, program_memory_1_rd, program_memory_1_ro1, program_memory_1_ro2;
  wire [3:0] program_memory_1_opcode;
  wire [7:0] _2x8bit_mux_1_out, _4x8bit_mux_1_p3, _4x8bit_mux_1_p4, _4x8bit_mux_1_p6, program_memory_1_imm8,
       register_file_1_readp;
  wire [15:0] _2x16bit_mux_1_p4, _4x8bit_mux_1_p5, _4x16bit_mux_1_out, _16bit_incrementer_1_out,
       program_counter_1_r, program_memory_1_imm16;

  nand nand_1 (nand_1_out, clk_2, clk_2);
  program_memory program_memory_1 (
    .ADR(program_counter_1_r), .OPCODE(program_memory_1_opcode), .RD(program_memory_1_rd),
    .RO1(program_memory_1_ro1), .RO2(program_memory_1_ro2), .IMM8(program_memory_1_imm8),
    .IMM16(program_memory_1_imm16), .ALUOP(program_memory_1_aluop));  // open: COND
  program_counter program_counter_1 (.CLK(clk_2), .W(_4x16bit_mux_1_out), .R(program_counter_1_r));
  _4x16bit_mux _4x16bit_mux_1 (
    .SEL(nand_2_out), .IN0({16{1'b0}}), .IN1(_16bit_incrementer_1_out), .IN2(_4x8bit_mux_1_p5),
    .IN3(program_memory_1_imm16), .OUT(_4x16bit_mux_1_out));
  oprom oprom_1 (
    .OPCODE(program_memory_1_opcode), .SKIP(1'b0), .RWEN(oprom_1_rwen), .FWEN(oprom_1_fwen),
    .MWEN(oprom_1_mwen), .BSSEL(oprom_1_bssel), .MASSEL(oprom_1_massel), .RSSEL(oprom_1_rssel),
    .PCSSEL(oprom_1_pcssel));
  _16bit_incrementer _16bit_incrementer_1 (.IN(program_counter_1_r), .OUT(_16bit_incrementer_1_out));
  // _4x8bit_mux _4x8bit_mux_1: pin names not known; wires that end beside it: oprom_1_rssel, program_memory_1_imm8, _4x8bit_mux_1_p3, _4x8bit_mux_1_p4, _4x8bit_mux_1_p5[7:0], _4x8bit_mux_1_p6
  nand nand_2 (nand_2_out[1], nand_4_out, nand_4_out);
  nand nand_3 (nand_2_out[0], nand_5_out, nand_5_out);
  nand nand_4 (nand_4_out, RESET, oprom_1_pcssel[1]);
  nand nand_5 (nand_5_out, RESET, oprom_1_pcssel[0]);
  register_file register_file_1 (
    .CLK(nand_1_out), .WEN(oprom_1_rwen), .WRITE(_4x8bit_mux_1_p6), .R2SEL(program_memory_1_ro2),
    .R1SEL(program_memory_1_ro1), .WSEL(program_memory_1_rd), .READ1(_4x8bit_mux_1_p5[7:0]),
    .READ2(_4x8bit_mux_1_p5[15:8]), .READP(register_file_1_readp));
  // _2x16bit_mux _2x16bit_mux_1: pin names not known; wires that end beside it: oprom_1_massel, {register_file_1_readp, _4x8bit_mux_1_p5[7:0]}, program_memory_1_imm16, _2x16bit_mux_1_p4
  _2x8bit_mux _2x8bit_mux_1 (
    .SEL(oprom_1_bssel), .B(_4x8bit_mux_1_p5[15:8]), .A(program_memory_1_imm8), .OUT(_2x8bit_mux_1_out));
  nand nand_6 (nand_6_out, oprom_1_mwen, oprom_1_mwen);
  _8bit_alu _8bit_alu_1 (
    .A(_4x8bit_mux_1_p5[7:0]), .B(_2x8bit_mux_1_out), .OP(program_memory_1_aluop), .CLK(nand_1_out),
    .WFLAGEN(oprom_1_fwen), .RESULT(_4x8bit_mux_1_p4));  // open: FLAGS
  RAMDualPort #(.AddrBits(16), .Bits(8)) ramdualport_1 (
    .A(_2x16bit_mux_1_p4), .Din(_4x8bit_mux_1_p5[15:8]), .str(oprom_1_mwen), .C(clk), .ld(nand_6_out),
    .D(_4x8bit_mux_1_p3));

  // Notes on the sheet:
  //   clk: Hz: 100
endmodule
